// Logisim project Echo-8.circ as structural Verilog: 2 circuits, main circuit main
module main (
  output [7:0] out_1
);

  wire ADD, AND, CLK, clock_1_out, decoder_1_out1, decoder_1_out2, Get_Flag, HLT, Jump, Logic_Out, MOV_A,
       MOV_AC, MOV_B, MOV_BC, NOT, not_1_out, not_2_out, not_3_out, OR, Out_A, Out_B, Out_C, SUB;
  wire [7:0] adder_1_out, ALU_Out, and_1_out, BUS, controlled_buffer_2_out, controlled_buffer_12_out, Get_A,
       Get_B, Get_C, JMP, not_4_out, or_1_out, PC, register_1_q, register_5_q, Set_A, Set_B, subtractor_1_out;
  wire [7:1] controlled_buffer_10_out, controlled_buffer_11_out, controlled_buffer_15_out;
  wire [11:0] Decode;

  Clock clock_1 (.out(clock_1_out));
  assign CLK = not_1_out ? clock_1_out : 1'bz;  // Controlled_Buffer controlled_buffer_1
  not not_1 (not_1_out, HLT);
  assign controlled_buffer_2_out = not_2_out ? PC : 8'bz;  // Controlled_Buffer controlled_buffer_2
  assign controlled_buffer_2_out = Jump ? JMP : 8'bz;  // Controlled_Buffer controlled_buffer_3
  not not_2 (not_2_out, Jump);
  assign Set_A = MOV_A ? Get_B : 8'bz;  // Controlled_Buffer controlled_buffer_4
  assign Set_B = MOV_B ? Get_A : 8'bz;  // Controlled_Buffer controlled_buffer_5
  assign Set_A = MOV_AC ? Get_C : 8'bz;  // Controlled_Buffer controlled_buffer_6
  assign Set_B = MOV_BC ? Get_C : 8'bz;  // Controlled_Buffer controlled_buffer_7
  not not_3 (not_3_out, Jump);
  Register register_1 (.D(controlled_buffer_2_out), .Q(register_1_q), .clk(CLK));  // open: en, clr
  ROM #(.dataWidth(12)) rom_1 (.addr(PC), .data(Decode));  // open: sel
  Adder adder_1 (.a(Get_A), .b(Get_B), .out(adder_1_out));  // open: cin, cout
  assign ALU_Out = ADD ? adder_1_out : 8'bz;  // Controlled_Buffer controlled_buffer_8
  assign ALU_Out = SUB ? subtractor_1_out : 8'bz;  // Controlled_Buffer controlled_buffer_9
  Subtractor subtractor_1 (.a(Get_A), .b(Get_B), .out(subtractor_1_out));  // open: bin, bout
  Counter counter_1 (.Increment(not_3_out), .In(register_1_q), .Clock(CLK), .Out(PC));
  Hex_Digit_Display hex_digit_display_1 (.value(BUS[7:4]));  // open: dp
  LED led_1 (.in(BUS[7]));
  LED led_2 (.in(BUS[6]));
  Hex_Digit_Display hex_digit_display_2 (.value(BUS[3:0]));  // open: dp
  LED led_3 (.in(HLT));
  assign and_1_out = Get_A & Get_B;  // AND_Gate and_1, 8 bits wide
  assign {controlled_buffer_10_out, Logic_Out} = AND ? and_1_out : 8'bz;  // Controlled_Buffer controlled_buffer_10
  assign or_1_out = Get_A | Get_B;  // OR_Gate or_1, 8 bits wide
  assign {controlled_buffer_11_out, Logic_Out} = OR ? or_1_out : 8'bz;  // Controlled_Buffer controlled_buffer_11
  assign controlled_buffer_12_out = Out_A ? Get_A : 8'bz;  // Controlled_Buffer controlled_buffer_12
  assign controlled_buffer_12_out = Out_B ? Get_B : 8'bz;  // Controlled_Buffer controlled_buffer_13
  assign controlled_buffer_12_out = Out_C ? Get_C : 8'bz;  // Controlled_Buffer controlled_buffer_14
  LED led_4 (.in(BUS[5]));
  LED led_5 (.in(BUS[2]));
  LED led_6 (.in(BUS[3]));
  LED led_7 (.in(BUS[4]));
  LED led_8 (.in(Get_B[7]));
  LED led_9 (.in(PC[7]));
  LED led_10 (.in(BUS[1]));
  LED led_11 (.in(BUS[0]));
  LED led_12 (.in(Get_B[3]));
  LED led_13 (.in(Get_B[6]));
  LED led_14 (.in(Get_B[4]));
  LED led_15 (.in(Get_B[5]));
  Register register_2 (.D(controlled_buffer_12_out), .Q(out_1), .clk(CLK));  // open: en, clr
  LED led_16 (.in(PC[4]));
  LED led_17 (.in(PC[5]));
  LED led_18 (.in(PC[6]));
  LED led_19 (.in(Get_B[2]));
  LED led_20 (.in(Get_B[1]));
  LED led_21 (.in(Get_B[0]));
  assign BUS[3:0] = out_1[3:0];  // Buffer buffer_1, 4 bits wide
  assign BUS[7:4] = out_1[7:4];  // Buffer buffer_2, 4 bits wide
  LED led_22 (.in(PC[2]));
  LED led_23 (.in(PC[0]));
  LED led_24 (.in(PC[3]));
  LED led_25 (.in(PC[1]));
  LED led_26 (.in(Get_C[7]));
  LED led_27 (.in(Get_C[5]));
  LED led_28 (.in(Get_C[4]));
  LED led_29 (.in(Get_C[6]));
  assign not_4_out = ~Get_A;  // NOT_Gate not_4, 8 bits wide
  LED led_30 (.in(Get_A[5]));
  LED led_31 (.in(Get_A[6]));
  LED led_32 (.in(Get_A[7]));
  LED led_33 (.in(Get_C[3]));
  LED led_34 (.in(Get_C[1]));
  LED led_35 (.in(Get_C[2]));
  assign {controlled_buffer_15_out, Logic_Out} = OR ? not_4_out : 8'bz;  // Controlled_Buffer controlled_buffer_15
  LED led_36 (.in(Get_A[2]));
  LED led_37 (.in(Get_A[4]));
  LED led_38 (.in(Get_A[1]));
  LED led_39 (.in(Get_A[3]));
  LED led_40 (.in(Get_C[0]));
  LED led_41 (.in(Get_A[0]));
  LED led_42 (.in(CLK));
  Decoder #(.select(4)) decoder_1 (
    .out0(HLT), .out1(decoder_1_out1), .out2(decoder_1_out2), .out3(MOV_A), .out4(MOV_B), .out5(ADD),
    .out6(SUB), .out7(AND), .out8(OR), .out9(NOT), .out10(Jump), .out11(MOV_AC), .out12(MOV_BC),
    .out13(Out_A), .out14(Out_B), .out15(Out_C), .sel(Decode[11:8]));  // open: en
  assign Set_A = decoder_1_out1 ? Decode[7:0] : 8'bz;  // Controlled_Buffer controlled_buffer_16
  assign Set_B = decoder_1_out2 ? Decode[7:0] : 8'bz;  // Controlled_Buffer controlled_buffer_17
  assign JMP = Jump ? Decode[7:0] : 8'bz;  // Controlled_Buffer controlled_buffer_18
  Register #(.width(1)) register_3 (.D(Logic_Out), .Q(Get_Flag), .clk(CLK));  // open: en, clr
  Register register_4 (.D(ALU_Out), .Q(Get_C), .clk(CLK));  // open: en, clr
  Register register_5 (.D(Get_B), .Q(register_5_q), .clk(CLK));  // open: en, clr
  assign Set_A = MOV_A ? register_5_q : 8'bz;  // Controlled_Buffer controlled_buffer_19
  Register register_6 (.D(Set_A), .Q(Get_A), .clk(CLK));  // open: en, clr
  Register register_7 (.D(Set_B), .Q(Get_B), .clk(CLK));  // open: en, clr

  // Notes on the sheet:
  //   contents of rom_1 (hex, n*v repeats v):
  //   100 201 500 b00 f00 a00
endmodule

module Counter (
  input  Increment,
  input  [7:0] In,
  input  Clock,
  output [7:0] Out
);

  wire not_1_out;
  wire [7:0] adder_1_out, controlled_buffer_1_out;

  Adder adder_1 (.a(In), .b(8'h1), .out(adder_1_out));  // open: cin, cout
  assign controlled_buffer_1_out = not_1_out ? In : 8'bz;  // Controlled_Buffer controlled_buffer_1
  not not_1 (not_1_out, Increment);
  assign controlled_buffer_1_out = Increment ? adder_1_out : 8'bz;  // Controlled_Buffer controlled_buffer_2
  Register register_1 (.D(controlled_buffer_1_out), .Q(Out), .clk(Clock));  // open: en, clr
endmodule
